# Fritzing sketch circuit (saved by Fritzing 1.0.1rc)
breadboards: 1

parts:
  Mod1 = Raspberry Pi Pico
  S1 = Pushbutton [package="[THT]"]
  S2 = Pushbutton [package="[THT]"]
  8x8_LED_Modul_mit_MAX1 = 8x8 LED Modul mit MAX7219 [package=THT]

nets:
  N1: Mod1.pin_3, Mod1.pin_8, Mod1.pin_13, Mod1.pin_18, Mod1.pin_23, Mod1.pin_28, Mod1.pin_33, Mod1.pin_38, S1.Pin_1, S1.Pin_2, S2.Pin_1, S2.Pin_2, 8x8_LED_Modul_mit_MAX1.GND_Eingang
  N2: Mod1.pin_20, S2.Pin_3, S2.Pin_4
  N3: Mod1.pin_24, 8x8_LED_Modul_mit_MAX1.CLK_Eingang
  N4: Mod1.pin_25, 8x8_LED_Modul_mit_MAX1.DIN_Eingang
  N5: Mod1.pin_26, 8x8_LED_Modul_mit_MAX1.CS_Eingang
  N6: Mod1.pin_27, S1.Pin_3, S1.Pin_4
  N7: Mod1.pin_36, 8x8_LED_Modul_mit_MAX1.VCC_Eingang

notes:
  project02_max7219

custom parts:
  Raspberry Pi Pico: Raspberry Pi Pico. Based around the RP2040 microcontroller the Pico is a low cost microcontroller device bringing Raspberry Pi quality, cost, and easy of use to the microcontroller space. Jan 2021, Split part in to two versions: tht (this one) and SMD. This one will drill holes for a .1 in header in pcb to allow plugging in the module as well as providing pads to solder the module to the top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
