# Fritzing sketch circuit (saved by Fritzing 1.0.1rc)
breadboards: 1

parts:
  Mod1 = Raspberry Pi Pico
  S1 = Pushbutton [package="[THT]"]
  S2 = Pushbutton [package="[THT]"]
  U1 = 74HC595 [package="DIP16 [THT]"]
  D1 = LED_BARGRAPH_8 [package=led_bargaph_8]

nets:
  N1: Mod1.pin_3, Mod1.pin_8, Mod1.pin_13, Mod1.pin_18, Mod1.pin_23, Mod1.pin_28, Mod1.pin_33, Mod1.pin_38, S1.Pin_1, S1.Pin_2, S2.Pin_1, S2.Pin_2, U1.GND, U1.MR, D1.A_A, D1.B_A, D1.C_A, D1.D_A, D1.E_A, D1.F_A, D1.G_A, D1.H_A
  N2: Mod1.pin_20, S2.Pin_3, S2.Pin_4
  N3: Mod1.pin_24, U1.SH_CP
  N4: Mod1.pin_25, U1.DS
  N5: Mod1.pin_26, U1.ST_CP
  N6: Mod1.pin_27, S1.Pin_3, S1.Pin_4
  N7: Mod1.pin_29, U1.OE
  N8: Mod1.pin_36, U1.VCC
  N9: U1.Q1, D1.B_C
  N10: U1.Q2, D1.C_C
  N11: U1.Q3, D1.D_C
  N12: U1.Q4, D1.E_C
  N13: U1.Q5, D1.F_C
  N14: U1.Q6, D1.G_C
  N15: U1.Q7, D1.H_C
  N16: U1.Q0, D1.A_C

notes:
  project04_hc595
  Connection details
  SER -> SPI0 TX (GP19) (Orange)
  SRCLK -> SPI0 SCK (GP18) (Green)
  Latch (SRCLK) -> GP20 (Yellow)
  OE -> GP22 (Grey)
  SRCLR -> GND (Black)
  Qa -> D1
  Qb -> D2
  Qc -> D3
  Qd -> D4
  Qe -> D5
  Qf -> D6
  Qg -> D7
  Qh -> D8

custom parts:
  Raspberry Pi Pico: Raspberry Pi Pico. Based around the RP2040 microcontroller the Pico is a low cost microcontroller device bringing Raspberry Pi quality, cost, and easy of use to the microcontroller space. Jan 2021, Split part in to two versions: tht (this one) and SMD. This one will drill holes for a .1 in header in pcb to allow plugging in the module as well as providing pads to solder the module to the top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
  LED_BARGRAPH_8: 8-Segment LED Bar Graph
